# Fritzing sketch SmartLetterboxController (saved by Fritzing 0.9.2b)
circuit board: 8.46667cm x 5.64444cm
breadboards: 1

parts:
  U1 = NodeMCU V1.0
  DHT1 = DHT22 Humidity and Temperature Sensor
  R1 = Resistor [tolerance=±5% resistance=10k package=THT]
  S1 = SWITCH-MOMENTARY-2 [package=tactile-pth-12mm]

nets:
  N1: U1.D2, DHT1.DATA
  3.3V: U1.3V3, DHT1.VDD, S1.1
  N2: U1.D6, R1.Pin_0, S1.2
  GND: U1.Vin, DHT1.GND, R1.Pin_1

custom parts:
  NodeMCU V1.0: ESP9266 based NodeMCU
