# Fritzing sketch LetterSensor_IRBreakBeam (saved by Fritzing 0.9.2b)
circuit board: 8.46667cm x 5.64444cm
breadboards: 1

parts:
  U1 = NodeMCU V1.0
  DHT1 = DHT22 Humidity and Temperature Sensor
  ReceiverBottom = TSOP312.., 314.. [package=THT]
  EmitterBottom = LTE-302 [package=lte-302]
  ReceiverTop = TSOP312.., 314.. [package=THT]
  EmitterTop = LTE-302 [package=lte-302]
  R3 = Resistor [tolerance=±5% resistance=1k package=THT]
  Sensor_Detected_LED = LED - 5mm [color="Red (633nm)" package="5 mm [THT]"]

nets:
  N1: U1.D2, DHT1.DATA
  N2: U1.D4, ReceiverTop.Data
  3.3V: U1.3V3, DHT1.VDD, ReceiverBottom.Vs, EmitterBottom.A, ReceiverTop.Vs, EmitterTop.A, R3.Pin_1
  N3: U1.D6, ReceiverBottom.Data
  N4: U1.D7, R3.Pin_0, Sensor_Detected_LED.anode
  GND: U1.Vin, DHT1.GND, ReceiverBottom.GND, EmitterBottom.C, ReceiverTop.GND, EmitterTop.C, Sensor_Detected_LED.cathode

custom parts:
  NodeMCU V1.0: ESP9266 based NodeMCU
